# Fritzing sketch RobotArmArduino (saved by Fritzing 0.9.3b)
breadboards: 1

parts:
  Part6 = Arduino Uno (Rev3)  # not connected
  J2 = Basic Servo
  J3 = Basic Servo
  J4 = Basic Servo
  J5 = Basic Servo
  JACK2 = 2.1mm Barrel Jack with Terminal Block
  BT1 = Bluetooth HC-06u [package=THT]  # not connected

nets:
  GND: J2.gnd, J3.gnd, J4.gnd, J5.gnd, JACK2.NEG
  VCC: J2.vcc, J3.vcc, J4.vcc, J5.vcc, JACK2.POS

custom parts:
  Bluetooth HC-06u: Bluetooth HC-06 - face up, pins down 16.5mm x 37.5mm PCB
